# Fritzing sketch arduinoisp (saved by Fritzing 0.9.2b)
breadboards: 1

parts:
  U1 = attiny85 [package=dip]
  Part1 = Arduino Uno (Rev3) - ICSP
  C1 = Electrolytic Capacitor [capacitance=10µF package="100 mil [THT, electrolytic]"]

nets:
  N1: U1.Pin_1, Part1.D10_PWM/SS
  N2: U1.Pin_4, Part1.GND, C1.-
  N3: U1.Pin_5, Part1.D11_PWM/MOSI
  N4: U1.Pin_6, Part1.D12/MISO
  N5: U1.Pin_7, Part1.D13/SCK
  N6: U1.Pin_8, Part1.5V
  N7: Part1.IOREF, C1.+
