# Fritzing sketch sketch (saved by Fritzing 0.9.2b)
breadboards: 1

parts:
  U1 = attiny85 [package=dip]
  L1 = Inductor [package="0805 [SMD]"]

nets:
  N1: U1.Pin_2, L1.pin_1
  N2: U1.Pin_3, L1.pin_0
